// Logisim project exp-1.circ as structural Verilog: 1 circuit, main circuit main
module main (
  input  in_1,
  input  in_2,
  input  in_3,
  input  in_4,
  input  in_5,
  input  in_6,
  input  in_7,
  input  in_8,
  input  in_9,
  input  in_10,
  input  in_11,
  input  in_12,
  input  in_13,
  output out_14,
  output out_15,
  output out_16,
  output out_17,
  output out_18,
  output out_19,
  output out_20
);

  and and_1 (out_14, in_1, in_3);
  or or_1 (out_16, in_5, in_7);
  not not_1 (out_18, in_9);
  nand nand_1 (out_20, in_11, in_13);
  nor nor_1 (out_15, in_2, in_4);
  xor xor_1 (out_17, in_6, in_8);
  xnor xnor_1 (out_19, in_10, in_12);
endmodule
