// Logisim project exp-10.circ as structural Verilog: 1 circuit, main circuit main
module main (
  input  [3:0] in_1,
  input  Enable,
  input  [1:0] Set_01,
  input  [3:0] in_4,
  input  [1:0] Set_11,
  input  [3:0] in_6,
  input  [1:0] Set_01_2,
  input  [2:0] Set_000,
  output [3:0] A3_A2_A1_A0,
  output [3:0] A3_A2_A1__new_A,
  output [3:0] _0_0_0_A0,
  output [1:0] Q0_Q_1,
  output [3:0] A0_0_0_0,
  output [3:0] _0_Q3_Q2_Q1,
  output [3:0] New_Q_A0_Q3_Q2_Q1
);

  wire CLK_out, comparator_1_eq, not_1_out, register_4_q;
  wire [1:0] bit_extender_1_out, bit_extender_2_out, shifter_2_out;
  wire [2:0] Q_q;
  wire [3:0] adder_1_out, controlled_buffer_1_out, controlled_buffer_2_out, register_1_q, register_2_q,
       register_3_q, subtractor_1_out;

  Clock CLK (.out(CLK_out));
  Register #(.width(4)) register_1 (.D(in_1), .en(Enable), .Q(register_1_q), .clk(CLK_out));  // open: clr
  Register #(.width(4)) register_2 (.D(in_4), .en(Enable), .Q(register_2_q), .clk(CLK_out));  // open: clr
  Register #(.width(4)) register_3 (.D(in_6), .en(Enable), .Q(register_3_q), .clk(CLK_out));  // open: clr
  assign bit_extender_1_out = {{1{1'b0}}, register_3_q[0]};  // Bit_Extender bit_extender_1
  Register #(.width(1)) register_4 (.D(register_3_q[0]), .en(Enable), .Q(register_4_q), .clk(CLK_out));  // open: clr
  Shifter #(.width(4), .shift("lr")) shifter_1 (.in(register_3_q), .\dist (Set_01_2), .out(_0_Q3_Q2_Q1));
  Counter #(.width(3), .max('h7)) Q (.load(1'b1), .count(1'b1), .Q(Q_q), .clk(CLK_out));  // open: D, carry, clr
  Adder #(.width(4)) adder_1 (.a(register_2_q), .b(register_1_q), .out(adder_1_out));  // open: cin, cout
  Subtractor #(.width(4)) subtractor_1 (.a(register_2_q), .b(register_1_q), .out(subtractor_1_out));  // open: bin, bout
  Shifter #(.width(2)) shifter_2 (.in(bit_extender_1_out), .\dist (1'b1), .out(shifter_2_out));
  assign bit_extender_2_out = {{1{1'b0}}, register_4_q};  // Bit_Extender bit_extender_2
  Comparator #(.width(3)) comparator_1 (.a(Q_q), .b(Set_000), .eq(comparator_1_eq));  // open: gt, lt
  Multiplexer #(.select(2), .width(4)) multiplexer_1 (
    .in0(register_2_q), .in1(adder_1_out), .in2(subtractor_1_out), .in3(register_2_q), .out(A3_A2_A1_A0),
    .sel(Q0_Q_1), .en(Enable));
  Adder #(.width(2)) adder_2 (.a(shifter_2_out), .b(bit_extender_2_out), .out(Q0_Q_1));  // open: cin, cout
  not not_1 (not_1_out, comparator_1_eq);
  Adder #(.width(4)) adder_3 (.a(A0_0_0_0), .b(_0_Q3_Q2_Q1), .out(New_Q_A0_Q3_Q2_Q1));  // open: cin, cout
  assign controlled_buffer_1_out = not_1_out ? New_Q_A0_Q3_Q2_Q1 : 4'bz;  // Controlled_Buffer controlled_buffer_1
  assign controlled_buffer_2_out = not_1_out ? A3_A2_A1__new_A : 4'bz;  // Controlled_Buffer controlled_buffer_2
  Shifter #(.width(4), .shift("ar")) shifter_3 (.in(A3_A2_A1_A0), .\dist (Set_01), .out(A3_A2_A1__new_A));
  assign _0_0_0_A0 = {{3{1'b0}}, A3_A2_A1_A0[0]};  // Bit_Extender bit_extender_3
  Shifter #(.width(4)) shifter_4 (.in(_0_0_0_A0), .\dist (Set_11), .out(A0_0_0_0));
endmodule
