// Logisim project exp-11.circ as structural Verilog: 1 circuit, main circuit main
module main (
  input  in_1,
  input  [3:0] in_2,
  input  [3:0] in_3,
  input  in_4,
  output [4:0] out_5,
  output out_6,
  output out_7,
  output [5:0] out_8
);

  wire and_1_out, and_2_out;

  or or_1 (out_7, out_5[4], and_1_out, and_2_out);
  and and_1 (and_1_out, out_5[3], out_5[2]);
  and and_2 (and_2_out, out_5[3], out_5[1]);
  Adder #(.width(4)) adder_1 (.a(in_2), .b(in_3), .out(out_5[3:0]), .cin(in_1), .cout(out_5[4]));
  Adder #(.width(5)) adder_2 (
    .a(out_5), .b({{2{in_4}}, {2{out_7}}, in_4}), .out(out_8[4:0]), .cout(out_8[5]));  // open: cin

  assign out_6 = out_5[0];
endmodule
