// Logisim project exp-12.circ as structural Verilog: 1 circuit, main circuit main
module main (
  input  [3:0] in_1,
  input  [3:0] in_2,
  input  in_3,
  input  in_4,
  output [3:0] out_5,
  output [3:0] out_6,
  output out_7,
  output out_8,
  output [3:0] out_9,
  output out_10,
  output [3:0] out_11
);

  wire adder_2_cout, and_1_out, and_2_out;
  wire [3:0] not_1_out;

  assign not_1_out = ~in_2;  // NOT_Gate not_1, 4 bits wide
  or or_1 (out_8, adder_2_cout, and_1_out, and_2_out);
  Adder #(.width(4)) adder_1 (.a(not_1_out), .b({1'b1, in_3, 1'b1, in_3}), .out(out_5));  // open: cin, cout
  and and_1 (and_1_out, out_6[3], out_6[2]);
  and and_2 (and_2_out, out_6[3], out_6[1]);
  Adder #(.width(4)) adder_2 (.a(in_1), .b(out_5), .out(out_6), .cout(adder_2_cout));  // open: cin
  Adder #(.width(4)) adder_3 (.a(out_6), .b({in_4, {2{out_8}}, in_4}), .out(out_9), .cout(out_10));  // open: cin
  Adder #(.width(4)) adder_4 (.a(out_9), .b(4'b0001), .out(out_11));  // open: cin, cout

  assign out_7 = out_6[0];
endmodule
