// Logisim project exp-2.circ as structural Verilog: 1 circuit, main circuit main
module main (
  input  shift,
  input  [1:0] select_lines,
  input  enable,
  input  [3:0] Y3_Y2_Y1_Y0,
  input  Load,
  input  Load_2,
  input  Load_3,
  input  Load_4,
  input  Shift_2,
  output [3:0] out_10,
  output [3:0] D3_D2_D1_D0,
  output [3:0] C3_C2_C1_C0,
  output [3:0] B3_B2_B1_B0,
  output [3:0] A3_A2_A1_A0
);

  wire CLK_out, clock_1_out, REG_A_q0, REG_A_q1, REG_A_q2, REG_A_q3, REG_B_q0, REG_B_q1, REG_B_q2, REG_B_q3,
       REG_C_q0, REG_C_q1, REG_C_q2, REG_C_q3, REG_D_q0, REG_D_q1, REG_D_q2, REG_D_q3;

  Clock clock_1 (.out(clock_1_out));
  Shift_Register #(.length(4)) REG_D (
    .shift(shift), .clk(clock_1_out), .q0(REG_D_q0), .q1(REG_D_q1), .q2(REG_D_q2), .q3(REG_D_q3));  // open: in, out, load, clr, d0, d1, d2, d3
  Shift_Register #(.length(4)) REG_D_2 (
    .shift(Shift_2), .clk(CLK_out), .load(Load), .d0(Y3_Y2_Y1_Y0[3]), .q0(D3_D2_D1_D0[3]),
    .d1(Y3_Y2_Y1_Y0[2]), .q1(D3_D2_D1_D0[2]), .d2(Y3_Y2_Y1_Y0[1]), .q2(D3_D2_D1_D0[1]), .d3(Y3_Y2_Y1_Y0[0]),
    .q3(D3_D2_D1_D0[0]));  // open: in, out, clr
  Clock CLK (.out(CLK_out));
  Shift_Register #(.length(4)) REG_C (
    .shift(shift), .clk(clock_1_out), .q0(REG_C_q0), .q1(REG_C_q1), .q2(REG_C_q2), .q3(REG_C_q3));  // open: in, out, load, clr, d0, d1, d2, d3
  Shift_Register #(.length(4)) REG_C_2 (
    .shift(Shift_2), .clk(CLK_out), .load(Load_2), .d0(Y3_Y2_Y1_Y0[3]), .q0(C3_C2_C1_C0[3]),
    .d1(Y3_Y2_Y1_Y0[2]), .q1(C3_C2_C1_C0[2]), .d2(Y3_Y2_Y1_Y0[1]), .q2(C3_C2_C1_C0[1]), .d3(Y3_Y2_Y1_Y0[0]),
    .q3(C3_C2_C1_C0[0]));  // open: in, out, clr
  Shift_Register #(.length(4)) REG_B (
    .shift(shift), .clk(clock_1_out), .q0(REG_B_q0), .q1(REG_B_q1), .q2(REG_B_q2), .q3(REG_B_q3));  // open: in, out, load, clr, d0, d1, d2, d3
  Shift_Register #(.length(4)) REG_A (
    .shift(shift), .clk(clock_1_out), .q0(REG_A_q0), .q1(REG_A_q1), .q2(REG_A_q2), .q3(REG_A_q3));  // open: in, out, load, clr, d0, d1, d2, d3
  Shift_Register #(.length(4)) REG_B_2 (
    .shift(Shift_2), .clk(CLK_out), .load(Load_3), .d0(Y3_Y2_Y1_Y0[3]), .q0(B3_B2_B1_B0[3]),
    .d1(Y3_Y2_Y1_Y0[2]), .q1(B3_B2_B1_B0[2]), .d2(Y3_Y2_Y1_Y0[1]), .q2(B3_B2_B1_B0[1]), .d3(Y3_Y2_Y1_Y0[0]),
    .q3(B3_B2_B1_B0[0]));  // open: in, out, clr
  Shift_Register #(.length(4)) REG_A_2 (
    .shift(Shift_2), .clk(CLK_out), .load(Load_4), .d0(Y3_Y2_Y1_Y0[3]), .q0(A3_A2_A1_A0[3]),
    .d1(Y3_Y2_Y1_Y0[2]), .q1(A3_A2_A1_A0[2]), .d2(Y3_Y2_Y1_Y0[1]), .q2(A3_A2_A1_A0[1]), .d3(Y3_Y2_Y1_Y0[0]),
    .q3(A3_A2_A1_A0[0]));  // open: in, out, clr
  Multiplexer #(.select(2)) multiplexer_1 (
    .in0(REG_A_q3), .in1(REG_B_q3), .in2(REG_C_q3), .in3(REG_D_q3), .out(out_10[0]), .sel(select_lines),
    .en(enable));
  Multiplexer #(.select(2)) multiplexer_2 (
    .in0(REG_A_q2), .in1(REG_B_q2), .in2(REG_C_q2), .in3(REG_D_q2), .out(out_10[1]), .sel(select_lines),
    .en(enable));
  Multiplexer #(.select(2)) multiplexer_3 (
    .in0(REG_A_q1), .in1(REG_B_q1), .in2(REG_C_q1), .in3(REG_D_q1), .out(out_10[2]), .sel(select_lines),
    .en(enable));
  Multiplexer #(.select(2)) multiplexer_4 (
    .in0(REG_A_q0), .in1(REG_B_q0), .in2(REG_C_q0), .in3(REG_D_q0), .out(out_10[3]), .sel(select_lines),
    .en(enable));
endmodule
