// Logisim project exp-3.circ as structural Verilog: 1 circuit, main circuit main
module main (
  input  [2:0] S1_S0_Cin,
  input  Bit__0,
  input  [1:0] A1_A0,
  input  [1:0] B1_B0,
  input  ENABLE,
  output [2:0] Cout_D1_D0
);

  wire adder_1_cout, multiplexer_1_out, multiplexer_2_out, not_1_out, not_2_out, not_3_out;

  not not_1 (not_1_out, B1_B0[0]);
  not not_2 (not_2_out, Bit__0);
  not not_3 (not_3_out, B1_B0[1]);
  Multiplexer #(.select(2)) multiplexer_1 (
    .in0(B1_B0[0]), .in1(not_1_out), .in2(Bit__0), .in3(not_2_out), .out(multiplexer_1_out),
    .sel(S1_S0_Cin[2:1]), .en(ENABLE));
  Multiplexer #(.select(2)) multiplexer_2 (
    .in0(B1_B0[1]), .in1(not_3_out), .in2(Bit__0), .in3(not_2_out), .out(multiplexer_2_out),
    .sel(S1_S0_Cin[2:1]), .en(ENABLE));
  Adder #(.width(1)) adder_1 (
    .a(A1_A0[0]), .b(multiplexer_1_out), .out(Cout_D1_D0[0]), .cin(S1_S0_Cin[0]), .cout(adder_1_cout));
  Adder #(.width(1)) adder_2 (
    .a(A1_A0[1]), .b(multiplexer_2_out), .out(Cout_D1_D0[1]), .cin(adder_1_cout), .cout(Cout_D1_D0[2]));

  // Notes on the sheet:
  //   B0
  //   B1
  //   S1 S0
  //   A0
  //   A1
  //   Cin
  //   D0
  //   D1
endmodule
