// Logisim project exp-4.circ as structural Verilog: 1 circuit, main circuit main
module main (
  input  A,
  input  B,
  input  [1:0] S1_S0,
  input  Enable,
  output out_5
);

  wire and_1_out, not_1_out, or_1_out, xor_1_out;

  and and_1 (and_1_out, A, B);
  or or_1 (or_1_out, A, B);
  xor xor_1 (xor_1_out, A, B);
  not not_1 (not_1_out, A);
  Multiplexer #(.select(2)) multiplexer_1 (
    .in0(and_1_out), .in1(or_1_out), .in2(xor_1_out), .in3(not_1_out), .out(out_5), .sel(S1_S0), .en(Enable));
endmodule
