// Logisim project exp-5.circ as structural Verilog: 1 circuit, main circuit main
module main (
  input  _0,
  input  _0_2,
  input  _0_3,
  input  [3:0] A3_A2_A1_A0,
  input  Not_used,
  input  Not_used_2,
  input  Enable,
  input  [3:0] S3_S2_S1_S0,
  output A3,
  output [3:0] D3_D2_D1_D0,
  output A3_2,
  output A0
);

  wire multiplexer_1_out;

  Multiplexer #(.select(3)) multiplexer_1 (
    .in0(_0), .in1(_0_2), .in2(A3_A2_A1_A0[3]), .in3(_0_3), .in4(A3_A2_A1_A0[3]), .in5(A3_A2_A1_A0[0]),
    .in6(Not_used), .in7(Not_used_2), .out(multiplexer_1_out), .sel(S3_S2_S1_S0[2:0]), .en(Enable));
  Multiplexer multiplexer_2 (
    .in0(multiplexer_1_out), .in1(A3_A2_A1_A0[1]), .out(D3_D2_D1_D0[0]), .sel(S3_S2_S1_S0[3]), .en(Enable));
  Multiplexer multiplexer_3 (
    .in0(A3_A2_A1_A0[0]), .in1(A3_A2_A1_A0[2]), .out(D3_D2_D1_D0[1]), .sel(S3_S2_S1_S0[3]), .en(Enable));
  Multiplexer multiplexer_4 (
    .in0(A3_A2_A1_A0[1]), .in1(A3_A2_A1_A0[3]), .out(D3_D2_D1_D0[2]), .sel(Enable), .en(Enable));
  Multiplexer multiplexer_5 (
    .in0(A3_A2_A1_A0[2]), .in1(multiplexer_1_out), .out(D3_D2_D1_D0[3]), .sel(S3_S2_S1_S0[3]), .en(Enable));

  assign A0 = A3_A2_A1_A0[0];
  assign A3 = A3_A2_A1_A0[3];
  assign A3_2 = A3_A2_A1_A0[3];
endmodule
