// Logisim project exp-6.circ as structural Verilog: 1 circuit, main circuit main
module main (
  input  [4:0] S3_S2_S1_S0_Cin,
  input  Bit__0,
  input  Enable,
  input  [3:0] A3_A2_A1_A0,
  input  [3:0] B3_B2_B1_B0,
  input  in_6,
  input  A4,
  output [4:0] out_8,
  output C1,
  output C2,
  output C3,
  output out_12
);

  wire adder_1_out, adder_2_out, adder_3_out, adder_4_out, and_1_out, and_2_out, and_3_out, and_4_out,
       multiplexer_1_out, multiplexer_2_out, multiplexer_3_out, multiplexer_4_out, multiplexer_5_out,
       multiplexer_6_out, multiplexer_7_out, multiplexer_8_out, not_1_out, not_2_out, not_3_out, not_4_out,
       not_5_out, not_6_out, not_7_out, not_8_out, not_9_out, not_10_out, not_11_out, not_12_out, or_1_out,
       or_2_out, or_3_out, or_4_out, xor_1_out, xor_2_out, xor_3_out, xor_4_out;

  not not_1 (not_1_out, B3_B2_B1_B0[0]);
  not not_2 (not_2_out, Bit__0);
  and and_1 (and_1_out, A3_A2_A1_A0[0], B3_B2_B1_B0[0]);
  or or_1 (or_1_out, A3_A2_A1_A0[0], B3_B2_B1_B0[0]);
  not not_3 (not_3_out, B3_B2_B1_B0[1]);
  not not_4 (not_4_out, Bit__0);
  and and_2 (and_2_out, A3_A2_A1_A0[1], B3_B2_B1_B0[1]);
  or or_2 (or_2_out, A3_A2_A1_A0[1], B3_B2_B1_B0[1]);
  not not_5 (not_5_out, B3_B2_B1_B0[2]);
  not not_6 (not_6_out, Bit__0);
  and and_3 (and_3_out, A3_A2_A1_A0[2], B3_B2_B1_B0[2]);
  or or_3 (or_3_out, A3_A2_A1_A0[2], B3_B2_B1_B0[2]);
  not not_7 (not_7_out, B3_B2_B1_B0[3]);
  not not_8 (not_8_out, Bit__0);
  and and_4 (and_4_out, A3_A2_A1_A0[3], B3_B2_B1_B0[3]);
  or or_4 (or_4_out, A3_A2_A1_A0[3], B3_B2_B1_B0[3]);
  Multiplexer #(.select(2)) multiplexer_1 (
    .in0(B3_B2_B1_B0[0]), .in1(not_1_out), .in2(Bit__0), .in3(not_2_out), .out(multiplexer_1_out),
    .sel(S3_S2_S1_S0_Cin[2:1]), .en(Enable));
  xor xor_1 (xor_1_out, A3_A2_A1_A0[0], B3_B2_B1_B0[0]);
  not not_9 (not_9_out, A3_A2_A1_A0[0]);
  Multiplexer #(.select(2)) multiplexer_2 (
    .in0(B3_B2_B1_B0[1]), .in1(not_3_out), .in2(Bit__0), .in3(not_4_out), .out(multiplexer_2_out),
    .sel(S3_S2_S1_S0_Cin[2:1]), .en(Enable));
  xor xor_2 (xor_2_out, A3_A2_A1_A0[1], B3_B2_B1_B0[1]);
  not not_10 (not_10_out, A3_A2_A1_A0[1]);
  Multiplexer #(.select(2)) multiplexer_3 (
    .in0(B3_B2_B1_B0[2]), .in1(not_5_out), .in2(Bit__0), .in3(not_6_out), .out(multiplexer_3_out),
    .sel(S3_S2_S1_S0_Cin[2:1]), .en(Enable));
  xor xor_3 (xor_3_out, A3_A2_A1_A0[2], B3_B2_B1_B0[2]);
  not not_11 (not_11_out, A3_A2_A1_A0[2]);
  Multiplexer #(.select(2)) multiplexer_4 (
    .in0(B3_B2_B1_B0[3]), .in1(not_7_out), .in2(Bit__0), .in3(not_8_out), .out(multiplexer_4_out),
    .sel(S3_S2_S1_S0_Cin[2:1]), .en(Enable));
  xor xor_4 (xor_4_out, A3_A2_A1_A0[3], B3_B2_B1_B0[3]);
  not not_12 (not_12_out, A3_A2_A1_A0[3]);
  Adder #(.width(1)) adder_1 (
    .a(A3_A2_A1_A0[0]), .b(multiplexer_1_out), .out(adder_1_out), .cin(S3_S2_S1_S0_Cin[0]), .cout(C1));
  Multiplexer #(.select(2)) multiplexer_5 (
    .in0(and_1_out), .in1(or_1_out), .in2(xor_1_out), .in3(not_9_out), .out(multiplexer_5_out),
    .sel(S3_S2_S1_S0_Cin[2:1]), .en(Enable));
  Adder #(.width(1)) adder_2 (.a(A3_A2_A1_A0[1]), .b(multiplexer_2_out), .out(adder_2_out), .cin(C1), .cout(C2));
  Multiplexer #(.select(2)) multiplexer_6 (
    .in0(and_2_out), .in1(or_2_out), .in2(xor_2_out), .in3(not_10_out), .out(multiplexer_6_out),
    .sel(S3_S2_S1_S0_Cin[2:1]), .en(Enable));
  Adder #(.width(1)) adder_3 (.a(A3_A2_A1_A0[2]), .b(multiplexer_3_out), .out(adder_3_out), .cin(C2), .cout(C3));
  Multiplexer #(.select(2)) multiplexer_7 (
    .in0(and_3_out), .in1(or_3_out), .in2(xor_3_out), .in3(not_11_out), .out(multiplexer_7_out),
    .sel(S3_S2_S1_S0_Cin[2:1]), .en(Enable));
  Adder #(.width(1)) adder_4 (.a(A3_A2_A1_A0[3]), .b(multiplexer_4_out), .out(adder_4_out), .cin(C3), .cout(out_8[4]));
  Multiplexer #(.select(2)) multiplexer_8 (
    .in0(and_4_out), .in1(or_4_out), .in2(xor_4_out), .in3(not_12_out), .out(multiplexer_8_out),
    .sel(S3_S2_S1_S0_Cin[2:1]), .en(Enable));
  Multiplexer #(.select(2)) multiplexer_9 (
    .in0(adder_1_out), .in1(multiplexer_5_out), .in2(in_6), .in3(A3_A2_A1_A0[1]), .out(out_8[0]),
    .sel(S3_S2_S1_S0_Cin[4:3]), .en(Enable));
  Multiplexer #(.select(2)) multiplexer_10 (
    .in0(adder_2_out), .in1(multiplexer_6_out), .in2(A3_A2_A1_A0[0]), .in3(A3_A2_A1_A0[2]), .out(out_8[1]),
    .sel(S3_S2_S1_S0_Cin[4:3]), .en(Enable));
  Multiplexer #(.select(2)) multiplexer_11 (
    .in0(adder_3_out), .in1(multiplexer_7_out), .in2(A3_A2_A1_A0[1]), .in3(A3_A2_A1_A0[3]), .out(out_8[2]),
    .sel(S3_S2_S1_S0_Cin[4:3]), .en(Enable));
  Multiplexer #(.select(2)) multiplexer_12 (
    .in0(adder_4_out), .in1(multiplexer_8_out), .in2(A3_A2_A1_A0[2]), .in3(A4), .out(out_8[3]),
    .sel(S3_S2_S1_S0_Cin[4:3]), .en(Enable));

  assign out_12 = out_8[4];

  // Notes on the sheet:
  //   A0
  //   B0
  //   A1
  //   B1
  //   A2
  //   B2
  //   A3
  //   B3
endmodule
