// Logisim project exp-7.circ as structural Verilog: 1 circuit, main circuit main
module main (
  input  [1:0] A1_A0,
  input  [1:0] B1_B0,
  output [3:0] C3_C2_C1_C0
);

  wire adder_1_cout, and_2_out, and_3_out, and_4_out;

  and and_1 (C3_C2_C1_C0[0], A1_A0[0], B1_B0[0]);
  and and_2 (and_2_out, A1_A0[1], B1_B0[0]);
  and and_3 (and_3_out, A1_A0[0], B1_B0[1]);
  and and_4 (and_4_out, A1_A0[1], B1_B0[1]);
  Adder #(.width(1)) adder_1 (.a(and_3_out), .b(and_2_out), .out(C3_C2_C1_C0[1]), .cout(adder_1_cout));  // open: cin
  Adder #(.width(1)) adder_2 (
    .a(adder_1_cout), .b(and_4_out), .out(C3_C2_C1_C0[2]), .cout(C3_C2_C1_C0[3]));  // open: cin

  // Notes on the sheet:
  //   A0
  //   B0
  //   A1
  //   B0
  //   A0.B0
  //   A1.B0
  //   A0
  //   B1
  //   A1
  //   B1
  //   A0.B1
  //   A1.B1
endmodule
