// Logisim project exp-9.circ as structural Verilog: 1 circuit, main circuit main
module main (
  input  [3:0] in_1,
  input  [2:0] Set_001,
  input  Enable,
  input  [1:0] Set__11,
  input  [1:0] Set_01,
  input  [2:0] Set_000,
  output [3:0] out_7,
  output [4:0] out_8,
  output [3:0] out_9,
  output [3:0] out_10,
  output out_11,
  output [3:0] out_12,
  output [3:0] out_13,
  output [3:0] out_14,
  output [3:0] out_15
);

  wire Clock_out, comparator_1_eq, not_1_out;
  wire [2:0] set_q;
  wire [3:0] adder_1_out, controlled_buffer_1_out, controlled_buffer_2_out, M_q;
  wire [4:4] shifter_2_out;

  Clock Clock (.out(Clock_out));
  Counter #(.width(4), .max('hf)) M (.D(in_1), .count(Enable), .Q(M_q), .clk(Clock_out));  // open: load, carry, clr
  Counter #(.width(4), .max('hf)) M_2 (
    .D(controlled_buffer_2_out), .count(Enable), .Q(out_10), .clk(Clock_out));  // open: load, carry, clr
  Counter #(.width(4), .max('hf)) M_3 (
    .D(controlled_buffer_1_out), .count(Enable), .Q(out_12), .clk(Clock_out));  // open: load, carry, clr
  Adder #(.width(4)) adder_1 (.a(out_10), .b(M_q), .out(adder_1_out), .cout(out_8[4]));  // open: cin
  Shifter #(.width(4), .shift("lr")) shifter_1 (.in(out_12), .\dist (Set_01), .out(out_15));
  Multiplexer #(.width(4)) multiplexer_1 (.in0(out_10), .in1(adder_1_out), .out(out_8[3:0]), .sel(out_11), .en(Enable));
  and and_1 (out_11, out_12[0], 1'b1);
  Counter #(.width(3), .max('h7)) set (.load(1'b1), .count(1'b1), .Q(set_q), .clk(Clock_out));  // open: D, carry, clr
  Comparator #(.width(3)) comparator_1 (.a(set_q), .b(Set_000), .eq(comparator_1_eq));  // open: gt, lt
  not not_1 (not_1_out, comparator_1_eq);
  assign controlled_buffer_1_out = not_1_out ? out_14 : 4'bz;  // Controlled_Buffer controlled_buffer_1
  assign controlled_buffer_2_out = not_1_out ? out_7 : 4'bz;  // Controlled_Buffer controlled_buffer_2
  Shifter #(.width(5), .shift("lr")) shifter_2 (.in(out_8), .\dist (Set_001), .out({shifter_2_out[4], out_7}));
  assign out_9 = {{3{1'b0}}, out_8[0]};  // Bit_Extender bit_extender_1
  Adder #(.width(4)) adder_2 (.a(out_13), .b(out_15), .out(out_14));  // open: cin, cout
  Shifter #(.width(4)) shifter_3 (.in(out_9), .\dist (Set__11), .out(out_13));
endmodule
